# Fritzing sketch rasp-pi-led-fritzing (saved by Fritzing 0.9.2b)
breadboards: 1

parts:
  Raspberry_Pi1 = Raspberry Pi B rev2
  LED1 = LED - 3mm [color="Red (633nm)" package="3 mm [THT]"]
  R1 = Resistor [tolerance=±5% resistance=100 package=THT]

nets:
  N1: Raspberry_Pi1.GND, LED1.cathode
  N2: Raspberry_Pi1.GPIO_4, R1.Pin_1
  N3: LED1.anode, R1.Pin_0
